// Logisim project PipelinedSimpleLEGv8.circ as structural Verilog
module Control (
  input  [10:0] in_1,
  output Reg2Loc,
  output Branch,
  output MemRead,
  output MemtoReg,
  output [1:0] ALUOp0,
  output MemWrite,
  output ALUSrc,
  output RegWrite,
  output out_10
);

  wire and_1_out, and_2_out, and_3_out, and_4_out, and_5_out, and_6_out, and_7_out, and_8_out, and_9_out,
       nor_1_out, nor_2_out, nor_3_out, nor_4_out, nor_5_out, nor_6_out, nor_7_out, nor_8_out, nor_9_out,
       nor_10_out, not_1_out, not_2_out, not_3_out, not_4_out, not_5_out, not_6_out, not_7_out, not_8_out,
       not_9_out, not_10_out, not_11_out, not_12_out, not_13_out, not_14_out, not_15_out, not_16_out,
       not_17_out, not_18_out, not_19_out, not_20_out, not_21_out, not_22_out, not_23_out, not_24_out,
       not_25_out, not_26_out, not_27_out, or_1_out, or_2_out, or_3_out, or_4_out, or_5_out;

  not not_1 (not_1_out, in_1[5]);
  not not_2 (not_2_out, in_1[4]);
  not not_3 (not_3_out, in_1[3]);
  not not_4 (not_4_out, in_1[2]);
  not not_5 (not_5_out, in_1[0]);
  not not_6 (not_6_out, in_1[9]);
  not not_7 (not_7_out, in_1[8]);
  not not_8 (not_8_out, in_1[7]);
  not not_9 (not_9_out, in_1[5]);
  nor nor_1 (nor_1_out, in_1[2], in_1[1], in_1[0]);
  not not_10 (not_10_out, in_1[9]);
  not not_11 (not_11_out, in_1[6]);
  not not_12 (not_12_out, in_1[4]);
  not not_13 (not_13_out, in_1[3]);
  and and_1 (and_1_out, in_1[10], in_1[9], in_1[8], in_1[7], in_1[6], not_1_out, not_2_out);
  and and_2 (and_2_out, not_3_out, not_4_out, in_1[1], not_5_out);
  nor nor_2 (nor_2_out, in_1[3], in_1[2], in_1[1], in_1[0]);
  not not_14 (not_14_out, in_1[9]);
  not not_15 (not_15_out, in_1[7]);
  not not_16 (not_16_out, in_1[5]);
  not not_17 (not_17_out, in_1[3]);
  not not_18 (not_18_out, in_1[9]);
  not not_19 (not_19_out, in_1[8]);
  not not_20 (not_20_out, in_1[7]);
  not not_21 (not_21_out, in_1[5]);
  not not_22 (not_22_out, in_1[3]);
  not not_23 (not_23_out, in_1[8]);
  not not_24 (not_24_out, in_1[7]);
  not not_25 (not_25_out, in_1[5]);
  and and_3 (and_3_out, in_1[10], not_10_out, in_1[8], in_1[7], not_11_out, in_1[5], not_12_out, not_13_out);
  and and_4 (and_4_out, and_1_out, and_2_out);
  and and_5 (and_5_out, and_1_out, nor_2_out);
  and and_6 (and_6_out, in_1[10], not_14_out, in_1[8], not_15_out, in_1[6], not_16_out, in_1[4], not_17_out, nor_1_out);
  and and_7 (and_7_out, in_1[10], not_18_out, not_19_out, not_20_out, in_1[6], not_21_out, in_1[4], not_22_out, nor_1_out);
  and and_8 (and_8_out, in_1[10], in_1[9], not_23_out, not_24_out, in_1[6], not_25_out, in_1[4], in_1[3], nor_1_out);
  and and_9 (and_9_out, in_1[10], not_6_out, not_7_out, not_8_out, in_1[6], not_9_out, in_1[4], in_1[3], nor_1_out);
  or or_1 (or_1_out, and_4_out, and_5_out);
  or or_2 (or_2_out, and_6_out, and_7_out, and_8_out, and_9_out);
  nor nor_3 (nor_3_out, or_2_out, and_3_out, and_4_out);
  nor nor_4 (nor_4_out, or_2_out, and_3_out);
  nor nor_5 (nor_5_out, and_3_out, and_5_out);
  or or_3 (or_3_out, or_2_out, and_4_out);
  nor nor_6 (nor_6_out, or_2_out, and_3_out, or_1_out);
  not not_26 (not_26_out, or_2_out);
  or or_4 (or_4_out, and_3_out, or_1_out);
  nor nor_7 (nor_7_out, or_2_out, or_1_out);
  nor nor_8 (nor_8_out, or_2_out, and_3_out, and_5_out);
  not not_27 (not_27_out, or_2_out);
  and and_10 (MemtoReg, not_27_out, and_4_out);
  and and_11 (ALUOp0[0], and_3_out, nor_9_out);
  nor nor_9 (nor_9_out, or_2_out, or_1_out);
  and and_12 (ALUOp0[1], or_2_out, nor_10_out);
  nor nor_10 (nor_10_out, and_3_out, or_1_out);
  and and_13 (MemWrite, and_5_out, nor_3_out);
  and and_14 (ALUSrc, or_1_out, nor_4_out);
  and and_15 (RegWrite, nor_5_out, or_3_out);
  and and_16 (out_10, nor_6_out, or_5_out);
  or or_5 (or_5_out, in_1[10], in_1[9], in_1[8], in_1[7], in_1[6], in_1[5], in_1[4], in_1[3], in_1[2], in_1[1], in_1[0]);
  and and_17 (Reg2Loc, not_26_out, or_4_out);
  and and_18 (Branch, and_3_out, nor_7_out);
  and and_19 (MemRead, and_4_out, nor_8_out);

  // Notes on the sheet:
  //   31
  //   21
  //   ORR (R-Type)
  //   AND (R-Type)
  //   ADD (R-Type)
  //   180 (CBZ)
  //   1986 (Load)
  //   Load or Store
  //   1984 (Store)
  //   SUB (R-Type)
  //   R-Type
  //   ALUOp1
  //   Unknown Instruction
endmodule

// ALU_C
module ALU_Control (
  input  [1:0] I_30,
  input  [10:0] I_24,
  output [3:0] out_3
);

  wire and_1_out, and_2_out, and_3_out, not_1_out;

  and and_1 (and_1_out, I_30[1], I_24[9]);
  not not_1 (not_1_out, I_30[1]);
  and and_2 (and_2_out, I_30[1], I_24[3]);
  and and_3 (and_3_out, I_30[1], I_24[8]);
  or or_1 (out_3[2], I_30[0], and_1_out);
  or or_2 (out_3[1], not_1_out, and_2_out);
  or or_3 (out_3[0], I_30[0], and_3_out);

  assign out_3[3] = 1'b0;

  // Notes on the sheet:
  //   31-21
  //   I[29]
  //   ALUOp0
  //   MSB
  //   LSB
endmodule

// Sign
module Sign_Extender (
  input  [31:0] in_1,
  output [31:0] out_2
);

  wire and_1_out, and_2_out, and_3_out, and_4_out, and_5_out, and_6_out, and_7_out, demultiplexer_1_out0,
       demultiplexer_1_out1, demultiplexer_2_out0, demultiplexer_2_out1, demultiplexer_3_out0,
       demultiplexer_3_out1, demultiplexer_4_out0, demultiplexer_4_out1, demultiplexer_5_out0,
       demultiplexer_5_out1, demultiplexer_6_out0, demultiplexer_6_out1, demultiplexer_7_out0,
       demultiplexer_7_out1, demultiplexer_8_out0, demultiplexer_8_out1, demultiplexer_9_out0,
       demultiplexer_9_out1, nor_1_out, not_1_out, not_2_out, not_3_out, not_4_out, not_5_out, not_6_out,
       not_7_out, not_8_out, not_9_out, not_10_out, not_11_out, or_1_out;

  not not_1 (not_1_out, in_1[30]);
  not not_2 (not_2_out, in_1[27]);
  not not_3 (not_3_out, in_1[25]);
  not not_4 (not_4_out, in_1[24]);
  not not_5 (not_5_out, in_1[26]);
  not not_6 (not_6_out, in_1[25]);
  not not_7 (not_7_out, in_1[24]);
  not not_8 (not_8_out, in_1[23]);
  not not_9 (not_9_out, in_1[21]);
  and and_1 (and_1_out, in_1[31], not_1_out, in_1[29], in_1[28], not_2_out, in_1[26], not_3_out, not_4_out);
  and and_2 (and_2_out, in_1[31], in_1[30], in_1[29], in_1[28], in_1[27], not_5_out, not_6_out);
  and and_3 (and_3_out, not_7_out, not_8_out, in_1[22], not_9_out);
  nor nor_1 (nor_1_out, in_1[24], in_1[23], in_1[22], in_1[21]);
  and and_4 (and_4_out, and_2_out, and_3_out);
  or or_1 (or_1_out, and_4_out, and_5_out);
  and and_5 (and_5_out, and_2_out, nor_1_out);
  Demultiplexer #(.enable("false")) demultiplexer_1 (
    .out0(demultiplexer_1_out0), .out1(demultiplexer_1_out1), .in(in_1[20]), .sel(or_1_out));
  Demultiplexer #(.enable("false")) demultiplexer_2 (
    .out0(demultiplexer_2_out0), .out1(demultiplexer_2_out1), .in(in_1[19]), .sel(or_1_out));
  Demultiplexer #(.enable("false")) demultiplexer_3 (
    .out0(demultiplexer_3_out0), .out1(demultiplexer_3_out1), .in(in_1[18]), .sel(or_1_out));
  Demultiplexer #(.enable("false")) demultiplexer_4 (
    .out0(demultiplexer_4_out0), .out1(demultiplexer_4_out1), .in(in_1[17]), .sel(or_1_out));
  Demultiplexer #(.enable("false")) demultiplexer_5 (
    .out0(demultiplexer_5_out0), .out1(demultiplexer_5_out1), .in(in_1[16]), .sel(or_1_out));
  Demultiplexer #(.enable("false")) demultiplexer_6 (
    .out0(demultiplexer_6_out0), .out1(demultiplexer_6_out1), .in(in_1[15]), .sel(or_1_out));
  Demultiplexer #(.enable("false")) demultiplexer_7 (
    .out0(demultiplexer_7_out0), .out1(demultiplexer_7_out1), .in(in_1[14]), .sel(or_1_out));
  Demultiplexer #(.enable("false")) demultiplexer_8 (
    .out0(demultiplexer_8_out0), .out1(demultiplexer_8_out1), .in(in_1[13]), .sel(or_1_out));
  Demultiplexer #(.enable("false")) demultiplexer_9 (
    .out0(demultiplexer_9_out0), .out1(demultiplexer_9_out1), .in(in_1[12]), .sel(or_1_out));
  and and_6 (and_6_out, in_1[20], or_1_out, not_10_out);
  not not_10 (not_10_out, and_1_out);
  and and_7 (and_7_out, in_1[23], and_1_out, not_11_out);
  not not_11 (not_11_out, or_1_out);
  or or_2 (out_2[31], and_6_out, and_7_out);
  MUX_ish mux_ish_1 (
    .in_3(demultiplexer_1_out1), .in_4(demultiplexer_8_out0), .out_5(out_2[8]), .in_1(and_1_out),
    .in_2(or_1_out));
  MUX_ish mux_ish_2 (
    .in_3(demultiplexer_2_out1), .in_4(demultiplexer_9_out0), .out_5(out_2[7]), .in_1(and_1_out),
    .in_2(or_1_out));
  MUX_ish mux_ish_3 (.in_3(demultiplexer_3_out1), .in_4(in_1[11]), .out_5(out_2[6]), .in_1(and_1_out), .in_2(or_1_out));
  MUX_ish mux_ish_4 (.in_3(demultiplexer_4_out1), .in_4(in_1[10]), .out_5(out_2[5]), .in_1(and_1_out), .in_2(or_1_out));
  MUX_ish mux_ish_5 (.in_3(demultiplexer_5_out1), .in_4(in_1[9]), .out_5(out_2[4]), .in_1(and_1_out), .in_2(or_1_out));
  MUX_ish mux_ish_6 (.in_3(demultiplexer_6_out1), .in_4(in_1[8]), .out_5(out_2[3]), .in_1(and_1_out), .in_2(or_1_out));
  MUX_ish mux_ish_7 (.in_3(demultiplexer_7_out1), .in_4(in_1[7]), .out_5(out_2[2]), .in_1(and_1_out), .in_2(or_1_out));
  MUX_ish mux_ish_8 (.in_3(demultiplexer_8_out1), .in_4(in_1[6]), .out_5(out_2[1]), .in_1(and_1_out), .in_2(or_1_out));
  MUX_ish mux_ish_9 (.in_3(demultiplexer_9_out1), .in_4(in_1[5]), .out_5(out_2[0]), .in_1(and_1_out), .in_2(or_1_out));
  MUX_ish mux_ish_10 (.in_3(out_2[31]), .in_4(in_1[23]), .out_5(out_2[18]), .in_1(and_1_out), .in_2(or_1_out));
  MUX_ish mux_ish_11 (.in_3(out_2[31]), .in_4(in_1[22]), .out_5(out_2[17]), .in_1(and_1_out), .in_2(or_1_out));
  MUX_ish mux_ish_12 (.in_3(out_2[31]), .in_4(in_1[21]), .out_5(out_2[16]), .in_1(and_1_out), .in_2(or_1_out));
  MUX_ish mux_ish_13 (
    .in_3(out_2[31]), .in_4(demultiplexer_1_out0), .out_5(out_2[15]), .in_1(and_1_out), .in_2(or_1_out));
  MUX_ish mux_ish_14 (
    .in_3(out_2[31]), .in_4(demultiplexer_2_out0), .out_5(out_2[14]), .in_1(and_1_out), .in_2(or_1_out));
  MUX_ish mux_ish_15 (
    .in_3(out_2[31]), .in_4(demultiplexer_3_out0), .out_5(out_2[13]), .in_1(and_1_out), .in_2(or_1_out));
  MUX_ish mux_ish_16 (
    .in_3(out_2[31]), .in_4(demultiplexer_4_out0), .out_5(out_2[12]), .in_1(and_1_out), .in_2(or_1_out));
  MUX_ish mux_ish_17 (
    .in_3(out_2[31]), .in_4(demultiplexer_5_out0), .out_5(out_2[11]), .in_1(and_1_out), .in_2(or_1_out));
  MUX_ish mux_ish_18 (
    .in_3(out_2[31]), .in_4(demultiplexer_6_out0), .out_5(out_2[10]), .in_1(and_1_out), .in_2(or_1_out));
  MUX_ish mux_ish_19 (
    .in_3(out_2[31]), .in_4(demultiplexer_7_out0), .out_5(out_2[9]), .in_1(and_1_out), .in_2(or_1_out));

  assign out_2[30:19] = {12{out_2[31]}};

  // Notes on the sheet:
  //   Opcode
  //   Branch Address Start
  //   Load Address Start
  //   Load Address End
  //   Branch Address End
  //   Sign Extend In
  //   31
  //   21
  //   20
  //   5
  //   Branch
  //   Load/Store
  //   Outputs 31-19
  //   Sign Extend Out
endmodule

module _4_1_MUX (
  input  in_1,
  input  in_2,
  input  in_3,
  input  in_4,
  input  in_5,
  input  in_6,
  output out_7
);

  wire and_1_out, and_2_out, and_3_out, and_4_out, not_1_out, not_2_out;

  not not_1 (not_1_out, in_2);
  not not_2 (not_2_out, in_1);
  and and_1 (and_1_out, in_3, not_1_out, not_2_out);
  and and_2 (and_2_out, in_4, not_1_out, in_1);
  and and_3 (and_3_out, in_5, in_2, not_2_out);
  and and_4 (and_4_out, in_6, in_2, in_1);
  or or_1 (out_7, and_1_out, and_2_out, and_3_out, and_4_out);
endmodule

module MUX_ish (
  input  in_1,
  input  in_2,
  input  in_3,
  input  in_4,
  output out_5
);

  wire and_1_out, and_2_out, not_1_out, not_2_out;

  not not_1 (not_1_out, in_2);
  not not_2 (not_2_out, in_1);
  and and_1 (and_1_out, in_3, in_2, not_2_out);
  and and_2 (and_2_out, in_4, in_1, not_1_out);
  or or_1 (out_5, and_1_out, and_2_out);
endmodule

// Shift
module Shift_Left_2 (
  input  [31:0] in_1,
  output [31:0] out_2
);


  assign out_2 = {in_1[29:0], 2'b00};

  // Notes on the sheet:
  //   Shift Left 2 In
  //   0-31
  //   Shift left 2 Out
endmodule

module ROM_CONTROL (
  input  in_1,
  input  in_2,
  input  in_3,
  input  in_4,
  input  in_5,
  input  in_6,
  input  in_7,
  input  in_8,
  input  in_9,
  input  in_10,
  input  in_11,
  output out_12,
  output out_13,
  output out_14,
  output out_15,
  output out_16,
  output out_17,
  output out_18,
  output out_19
);

  ROM #(.addrWidth(11)) rom_1 (
    .addr({in_11, in_10, in_9, in_8, in_7, in_6, in_5, in_4, in_3, in_2, in_1}),
    .data({out_19, out_18, out_17, out_16, out_15, out_14, out_13, out_12}));  // open: sel

  // Notes on the sheet:
  //   contents of rom_1 (hex, n*v repeats v):
  //   80*0 11 1904*0 15*11
endmodule

// Adder
module Add_Sub (
  input  Cin,
  input  A,
  input  B,
  input  Sub,
  output out_5,
  output out_6
);

  wire and_1_out, and_2_out, xor_1_out, xor_3_out;

  xor xor_1 (xor_1_out, B, Sub);
  and and_1 (and_1_out, A, xor_1_out);
  xor xor_2 (out_5, Cin, xor_3_out);
  and and_2 (and_2_out, Cin, xor_3_out);
  xor xor_3 (xor_3_out, A, xor_1_out);
  or or_1 (out_6, and_2_out, and_1_out);
endmodule

// 1B ALU
module _1_Bit_ALU (
  input  ALU_Cont_MSB,
  input  in_2,
  input  in_3,
  input  ALU_Cont_LSB,
  input  Cin,
  input  A,
  input  B,
  output Y,
  output Cout
);

  wire add_sub_1_out_5, alu_cont_in_1__0000, alu_cont_in_1__0001, alu_cont_in_1__0010, alu_cont_in_1__0110,
       alu_cont_in_1__0111, and_1_out, and_2_out, and_3_out, and_4_out, and_5_out, or_1_out, or_2_out;

  ALU_Cont_In alu_cont_in_1 (
    .ALU_Cont_MSB(ALU_Cont_MSB), .in_2(in_2), .in_3(in_3), ._0000(alu_cont_in_1__0000),
    ._0001(alu_cont_in_1__0001), ._0010(alu_cont_in_1__0010), ._0110(alu_cont_in_1__0110),
    ._0111(alu_cont_in_1__0111), .ALU_Cont_LSB(ALU_Cont_LSB));  // open: _0011, _0100, _0101, _1XXX
  and and_1 (and_1_out, A, B);
  or or_1 (or_1_out, A, B);
  or or_2 (or_2_out, alu_cont_in_1__0010, alu_cont_in_1__0110);
  Add_Sub add_sub_1 (.Cin(Cin), .A(A), .B(B), .Sub(alu_cont_in_1__0110), .out_5(add_sub_1_out_5), .out_6(Cout));
  and and_2 (and_2_out, and_1_out, alu_cont_in_1__0000);
  and and_3 (and_3_out, or_1_out, alu_cont_in_1__0001);
  and and_4 (and_4_out, alu_cont_in_1__0111, B);
  and and_5 (and_5_out, or_2_out, add_sub_1_out_5);
  or or_3 (Y, and_2_out, and_3_out, and_4_out, and_5_out);
endmodule

// ALU Cont Dec
module ALU_Cont_In (
  input  ALU_Cont_MSB,
  input  in_2,
  input  in_3,
  input  ALU_Cont_LSB,
  output _0000,
  output _0001,
  output _0010,
  output _0011,
  output _0100,
  output _0101,
  output _0110,
  output _0111,
  output _1XXX
);

  wire not_1_out, not_2_out, not_3_out, not_4_out;

  not not_1 (not_1_out, ALU_Cont_MSB);
  not not_2 (not_2_out, in_2);
  not not_3 (not_3_out, in_3);
  not not_4 (not_4_out, ALU_Cont_LSB);
  and and_1 (_0000, not_1_out, not_2_out, not_3_out, not_4_out);
  and and_2 (_0001, not_1_out, not_2_out, not_3_out, ALU_Cont_LSB);
  and and_3 (_0010, not_1_out, not_2_out, in_3, not_4_out);
  and and_4 (_0011, not_1_out, not_2_out, in_3, ALU_Cont_LSB);
  and and_5 (_0100, not_1_out, in_2, not_3_out, not_4_out);
  and and_6 (_0101, not_1_out, in_2, not_3_out, ALU_Cont_LSB);
  and and_7 (_0110, not_1_out, in_2, in_3, not_4_out);
  and and_8 (_0111, not_1_out, in_2, in_3, ALU_Cont_LSB);

  assign _1XXX = ALU_Cont_MSB;
endmodule

// ALU
module _32B_ALU (
  input  [3:0] LSB,
  input  [31:0] in_2,
  input  [31:0] in_3,
  output [31:0] out_4,
  output out_5
);

  wire and_1_out, n1_bit_alu_1_cout, n1_bit_alu_2_cout, n1_bit_alu_3_cout, n1_bit_alu_4_cout,
       n1_bit_alu_5_cout, n1_bit_alu_6_cout, n1_bit_alu_7_cout, n1_bit_alu_8_cout, n1_bit_alu_9_cout,
       n1_bit_alu_10_cout, n1_bit_alu_11_cout, n1_bit_alu_12_cout, n1_bit_alu_13_cout, n1_bit_alu_14_cout,
       n1_bit_alu_15_cout, n1_bit_alu_16_cout, n1_bit_alu_17_cout, n1_bit_alu_18_cout, n1_bit_alu_19_cout,
       n1_bit_alu_20_cout, n1_bit_alu_21_cout, n1_bit_alu_22_cout, n1_bit_alu_23_cout, n1_bit_alu_24_cout,
       n1_bit_alu_25_cout, n1_bit_alu_26_cout, n1_bit_alu_27_cout, n1_bit_alu_28_cout, n1_bit_alu_29_cout,
       n1_bit_alu_30_cout, n1_bit_alu_31_cout, nor_1_out;

  and and_1 (and_1_out, LSB[2], LSB[1], nor_1_out);
  nor nor_1 (nor_1_out, LSB[3], LSB[0]);
  _1_Bit_ALU u_1_bit_alu_1 (
    .ALU_Cont_MSB(LSB[3]), .in_2(LSB[2]), .in_3(LSB[1]), .Cin(and_1_out), .A(in_2[0]), .B(in_3[0]),
    .Y(out_4[0]), .Cout(n1_bit_alu_1_cout), .ALU_Cont_LSB(LSB[0]));
  _1_Bit_ALU u_1_bit_alu_2 (
    .ALU_Cont_MSB(LSB[3]), .in_2(LSB[2]), .in_3(LSB[1]), .Cin(n1_bit_alu_1_cout), .A(in_2[1]), .B(in_3[1]),
    .Y(out_4[1]), .Cout(n1_bit_alu_2_cout), .ALU_Cont_LSB(LSB[0]));
  _1_Bit_ALU u_1_bit_alu_3 (
    .ALU_Cont_MSB(LSB[3]), .in_2(LSB[2]), .in_3(LSB[1]), .Cin(n1_bit_alu_2_cout), .A(in_2[2]), .B(in_3[2]),
    .Y(out_4[2]), .Cout(n1_bit_alu_3_cout), .ALU_Cont_LSB(LSB[0]));
  nor nor_2 (out_5, out_4[0], out_4[1], out_4[2], out_4[3], out_4[4], out_4[5], out_4[6], out_4[7], out_4[8], out_4[9], out_4[10], out_4[11], out_4[12], out_4[13], out_4[14], out_4[15], out_4[16], out_4[17], out_4[18], out_4[19], out_4[20], out_4[21], out_4[22], out_4[23], out_4[24], out_4[25], out_4[26], out_4[27], out_4[28], out_4[29], out_4[30], out_4[31]);
  _1_Bit_ALU u_1_bit_alu_4 (
    .ALU_Cont_MSB(LSB[3]), .in_2(LSB[2]), .in_3(LSB[1]), .Cin(n1_bit_alu_3_cout), .A(in_2[3]), .B(in_3[3]),
    .Y(out_4[3]), .Cout(n1_bit_alu_4_cout), .ALU_Cont_LSB(LSB[0]));
  _1_Bit_ALU u_1_bit_alu_5 (
    .ALU_Cont_MSB(LSB[3]), .in_2(LSB[2]), .in_3(LSB[1]), .Cin(n1_bit_alu_4_cout), .A(in_2[4]), .B(in_3[4]),
    .Y(out_4[4]), .Cout(n1_bit_alu_5_cout), .ALU_Cont_LSB(LSB[0]));
  _1_Bit_ALU u_1_bit_alu_6 (
    .ALU_Cont_MSB(LSB[3]), .in_2(LSB[2]), .in_3(LSB[1]), .Cin(n1_bit_alu_5_cout), .A(in_2[5]), .B(in_3[5]),
    .Y(out_4[5]), .Cout(n1_bit_alu_6_cout), .ALU_Cont_LSB(LSB[0]));
  _1_Bit_ALU u_1_bit_alu_7 (
    .ALU_Cont_MSB(LSB[3]), .in_2(LSB[2]), .in_3(LSB[1]), .Cin(n1_bit_alu_6_cout), .A(in_2[6]), .B(in_3[6]),
    .Y(out_4[6]), .Cout(n1_bit_alu_7_cout), .ALU_Cont_LSB(LSB[0]));
  _1_Bit_ALU u_1_bit_alu_8 (
    .ALU_Cont_MSB(LSB[3]), .in_2(LSB[2]), .in_3(LSB[1]), .Cin(n1_bit_alu_7_cout), .A(in_2[7]), .B(in_3[7]),
    .Y(out_4[7]), .Cout(n1_bit_alu_8_cout), .ALU_Cont_LSB(LSB[0]));
  _1_Bit_ALU u_1_bit_alu_9 (
    .ALU_Cont_MSB(LSB[3]), .in_2(LSB[2]), .in_3(LSB[1]), .Cin(n1_bit_alu_8_cout), .A(in_2[8]), .B(in_3[8]),
    .Y(out_4[8]), .Cout(n1_bit_alu_9_cout), .ALU_Cont_LSB(LSB[0]));
  _1_Bit_ALU u_1_bit_alu_10 (
    .ALU_Cont_MSB(LSB[3]), .in_2(LSB[2]), .in_3(LSB[1]), .Cin(n1_bit_alu_9_cout), .A(in_2[9]), .B(in_3[9]),
    .Y(out_4[9]), .Cout(n1_bit_alu_10_cout), .ALU_Cont_LSB(LSB[0]));
  _1_Bit_ALU u_1_bit_alu_11 (
    .ALU_Cont_MSB(LSB[3]), .in_2(LSB[2]), .in_3(LSB[1]), .Cin(n1_bit_alu_10_cout), .A(in_2[10]),
    .B(in_3[10]), .Y(out_4[10]), .Cout(n1_bit_alu_11_cout), .ALU_Cont_LSB(LSB[0]));
  _1_Bit_ALU u_1_bit_alu_12 (
    .ALU_Cont_MSB(LSB[3]), .in_2(LSB[2]), .in_3(LSB[1]), .Cin(n1_bit_alu_11_cout), .A(in_2[11]),
    .B(in_3[11]), .Y(out_4[11]), .Cout(n1_bit_alu_12_cout), .ALU_Cont_LSB(LSB[0]));
  _1_Bit_ALU u_1_bit_alu_13 (
    .ALU_Cont_MSB(LSB[3]), .in_2(LSB[2]), .in_3(LSB[1]), .Cin(n1_bit_alu_12_cout), .A(in_2[12]),
    .B(in_3[12]), .Y(out_4[12]), .Cout(n1_bit_alu_13_cout), .ALU_Cont_LSB(LSB[0]));
  _1_Bit_ALU u_1_bit_alu_14 (
    .ALU_Cont_MSB(LSB[3]), .in_2(LSB[2]), .in_3(LSB[1]), .Cin(n1_bit_alu_13_cout), .A(in_2[13]),
    .B(in_3[13]), .Y(out_4[13]), .Cout(n1_bit_alu_14_cout), .ALU_Cont_LSB(LSB[0]));
  _1_Bit_ALU u_1_bit_alu_15 (
    .ALU_Cont_MSB(LSB[3]), .in_2(LSB[2]), .in_3(LSB[1]), .Cin(n1_bit_alu_14_cout), .A(in_2[14]),
    .B(in_3[14]), .Y(out_4[14]), .Cout(n1_bit_alu_15_cout), .ALU_Cont_LSB(LSB[0]));
  _1_Bit_ALU u_1_bit_alu_16 (
    .ALU_Cont_MSB(LSB[3]), .in_2(LSB[2]), .in_3(LSB[1]), .Cin(n1_bit_alu_15_cout), .A(in_2[15]),
    .B(in_3[15]), .Y(out_4[15]), .Cout(n1_bit_alu_16_cout), .ALU_Cont_LSB(LSB[0]));
  _1_Bit_ALU u_1_bit_alu_17 (
    .ALU_Cont_MSB(LSB[3]), .in_2(LSB[2]), .in_3(LSB[1]), .Cin(n1_bit_alu_16_cout), .A(in_2[16]),
    .B(in_3[16]), .Y(out_4[16]), .Cout(n1_bit_alu_17_cout), .ALU_Cont_LSB(LSB[0]));
  _1_Bit_ALU u_1_bit_alu_18 (
    .ALU_Cont_MSB(LSB[3]), .in_2(LSB[2]), .in_3(LSB[1]), .Cin(n1_bit_alu_17_cout), .A(in_2[17]),
    .B(in_3[17]), .Y(out_4[17]), .Cout(n1_bit_alu_18_cout), .ALU_Cont_LSB(LSB[0]));
  _1_Bit_ALU u_1_bit_alu_19 (
    .ALU_Cont_MSB(LSB[3]), .in_2(LSB[2]), .in_3(LSB[1]), .Cin(n1_bit_alu_18_cout), .A(in_2[18]),
    .B(in_3[18]), .Y(out_4[18]), .Cout(n1_bit_alu_19_cout), .ALU_Cont_LSB(LSB[0]));
  _1_Bit_ALU u_1_bit_alu_20 (
    .ALU_Cont_MSB(LSB[3]), .in_2(LSB[2]), .in_3(LSB[1]), .Cin(n1_bit_alu_19_cout), .A(in_2[19]),
    .B(in_3[19]), .Y(out_4[19]), .Cout(n1_bit_alu_20_cout), .ALU_Cont_LSB(LSB[0]));
  _1_Bit_ALU u_1_bit_alu_21 (
    .ALU_Cont_MSB(LSB[3]), .in_2(LSB[2]), .in_3(LSB[1]), .Cin(n1_bit_alu_20_cout), .A(in_2[20]),
    .B(in_3[20]), .Y(out_4[20]), .Cout(n1_bit_alu_21_cout), .ALU_Cont_LSB(LSB[0]));
  _1_Bit_ALU u_1_bit_alu_22 (
    .ALU_Cont_MSB(LSB[3]), .in_2(LSB[2]), .in_3(LSB[1]), .Cin(n1_bit_alu_21_cout), .A(in_2[21]),
    .B(in_3[21]), .Y(out_4[21]), .Cout(n1_bit_alu_22_cout), .ALU_Cont_LSB(LSB[0]));
  _1_Bit_ALU u_1_bit_alu_23 (
    .ALU_Cont_MSB(LSB[3]), .in_2(LSB[2]), .in_3(LSB[1]), .Cin(n1_bit_alu_22_cout), .A(in_2[22]),
    .B(in_3[22]), .Y(out_4[22]), .Cout(n1_bit_alu_23_cout), .ALU_Cont_LSB(LSB[0]));
  _1_Bit_ALU u_1_bit_alu_24 (
    .ALU_Cont_MSB(LSB[3]), .in_2(LSB[2]), .in_3(LSB[1]), .Cin(n1_bit_alu_23_cout), .A(in_2[23]),
    .B(in_3[23]), .Y(out_4[23]), .Cout(n1_bit_alu_24_cout), .ALU_Cont_LSB(LSB[0]));
  _1_Bit_ALU u_1_bit_alu_25 (
    .ALU_Cont_MSB(LSB[3]), .in_2(LSB[2]), .in_3(LSB[1]), .Cin(n1_bit_alu_24_cout), .A(in_2[24]),
    .B(in_3[24]), .Y(out_4[24]), .Cout(n1_bit_alu_25_cout), .ALU_Cont_LSB(LSB[0]));
  _1_Bit_ALU u_1_bit_alu_26 (
    .ALU_Cont_MSB(LSB[3]), .in_2(LSB[2]), .in_3(LSB[1]), .Cin(n1_bit_alu_25_cout), .A(in_2[25]),
    .B(in_3[25]), .Y(out_4[25]), .Cout(n1_bit_alu_26_cout), .ALU_Cont_LSB(LSB[0]));
  _1_Bit_ALU u_1_bit_alu_27 (
    .ALU_Cont_MSB(LSB[3]), .in_2(LSB[2]), .in_3(LSB[1]), .Cin(n1_bit_alu_26_cout), .A(in_2[26]),
    .B(in_3[26]), .Y(out_4[26]), .Cout(n1_bit_alu_27_cout), .ALU_Cont_LSB(LSB[0]));
  _1_Bit_ALU u_1_bit_alu_28 (
    .ALU_Cont_MSB(LSB[3]), .in_2(LSB[2]), .in_3(LSB[1]), .Cin(n1_bit_alu_27_cout), .A(in_2[27]),
    .B(in_3[27]), .Y(out_4[27]), .Cout(n1_bit_alu_28_cout), .ALU_Cont_LSB(LSB[0]));
  _1_Bit_ALU u_1_bit_alu_29 (
    .ALU_Cont_MSB(LSB[3]), .in_2(LSB[2]), .in_3(LSB[1]), .Cin(n1_bit_alu_28_cout), .A(in_2[28]),
    .B(in_3[28]), .Y(out_4[28]), .Cout(n1_bit_alu_29_cout), .ALU_Cont_LSB(LSB[0]));
  _1_Bit_ALU u_1_bit_alu_30 (
    .ALU_Cont_MSB(LSB[3]), .in_2(LSB[2]), .in_3(LSB[1]), .Cin(n1_bit_alu_29_cout), .A(in_2[29]),
    .B(in_3[29]), .Y(out_4[29]), .Cout(n1_bit_alu_30_cout), .ALU_Cont_LSB(LSB[0]));
  _1_Bit_ALU u_1_bit_alu_31 (
    .ALU_Cont_MSB(LSB[3]), .in_2(LSB[2]), .in_3(LSB[1]), .Cin(n1_bit_alu_30_cout), .A(in_2[30]),
    .B(in_3[30]), .Y(out_4[30]), .Cout(n1_bit_alu_31_cout), .ALU_Cont_LSB(LSB[0]));
  _1_Bit_ALU u_1_bit_alu_32 (
    .ALU_Cont_MSB(LSB[3]), .in_2(LSB[2]), .in_3(LSB[1]), .Cin(n1_bit_alu_31_cout), .A(in_2[31]),
    .B(in_3[31]), .Y(out_4[31]), .ALU_Cont_LSB(LSB[0]));  // open: Cout

  // Notes on the sheet:
  //   MSB
  //   A 0-31
  //   B 0-31
  //   Y 0-31
endmodule

// INST
module Instruction_memory (
  input  [31:0] in_1,
  output [31:0] out_2
);

  ROM #(.addrWidth(16), .dataWidth(32)) rom_1 (.addr(in_1[15:0]), .data(out_2));  // open: sel

  // Notes on the sheet:
  //   32 Bit address in
  //   contents of rom_1 (hex, n*v repeats v):
  //   4*0 f842802a 0 0 0 cb03004b 0 0 0 91005041 0 0 0 8b020061
  //   32 bit instruction out
endmodule

// DATA
module Data_Memory (
  input  [31:0] in_1,
  input  [31:0] in_2,
  input  MemWrite,
  input  MemRead,
  input  CLK,
  output [31:0] out_6
);

  wire and_1_out, and_2_out, xor_1_out;

  xor xor_1 (xor_1_out, MemWrite, MemRead);
  and and_1 (and_1_out, xor_1_out, MemWrite);
  and and_2 (and_2_out, xor_1_out, MemRead);
  RAM #(.addrWidth(16), .dataWidth(32), .bus("separate")) ram_1 (
    .addr(in_1[15:0]), .din(in_2), .data(out_6), .str(and_1_out), .clk(CLK), .ld(and_2_out));  // open: sel, clr

  // Notes on the sheet:
  //   Address
  //   Write Data
  //   Write
  //   Read
  //   Read Data
endmodule

// PC
module Program_Counter_w__Adders (
  input  in_1,
  input  [31:0] in_2,
  input  CLK,
  input  Reset,
  output [31:0] out_5
);

  wire [31:0] adder_1_out, adder_2_out, multiplexer_1_out;

  Register #(.width(32)) register_1 (.D(multiplexer_1_out), .Q(out_5), .clk(CLK), .clr(Reset));  // open: en
  Adder #(.width(32)) adder_1 (.a(out_5), .b(32'h4), .out(adder_1_out));  // open: cin, cout
  Adder #(.width(32)) adder_2 (.a(out_5), .b(in_2), .out(adder_2_out));  // open: cin, cout
  Multiplexer #(.width(32), .enable("false")) multiplexer_1 (
    .in0(adder_1_out), .in1(adder_2_out), .out(multiplexer_1_out), .sel(in_1));

  // Notes on the sheet:
  //   PC Output
  //   Sign Extended
  //   MUX Control
endmodule

// 31-21
module Instruction_Cutoff (
  input  [31:0] in_1,
  output [10:0] out_2
);


  assign out_2 = in_1[31:21];
endmodule

// Registers
module Register_File (
  input  [4:0] Read_Reg_Num_1,
  input  [4:0] Read_Reg_Num_2,
  input  [31:0] Write_Data,
  input  in_4,
  input  [4:0] Write_Reg,
  input  CLK,
  output [31:0] out_7,
  output [31:0] out_8
);

  wire and_1_out, and_2_out, and_3_out, and_4_out, and_5_out, and_6_out, and_7_out, and_8_out, and_9_out,
       and_10_out, and_11_out, and_12_out, and_13_out, and_14_out, and_15_out, and_16_out, and_17_out,
       and_18_out, and_19_out, and_20_out, and_21_out, and_22_out, and_23_out, and_24_out, and_25_out,
       and_26_out, and_27_out, and_28_out, and_29_out, and_30_out, and_31_out, and_32_out, decoder_1_out0,
       decoder_1_out1, decoder_1_out2, decoder_1_out3, decoder_1_out4, decoder_1_out5, decoder_1_out6,
       decoder_1_out7, decoder_1_out8, decoder_1_out9, decoder_1_out10, decoder_1_out11, decoder_1_out12,
       decoder_1_out13, decoder_1_out14, decoder_1_out15, decoder_1_out16, decoder_1_out17, decoder_1_out18,
       decoder_1_out19, decoder_1_out20, decoder_1_out21, decoder_1_out22, decoder_1_out23, decoder_1_out24,
       decoder_1_out25, decoder_1_out26, decoder_1_out27, decoder_1_out28, decoder_1_out29, decoder_1_out30,
       decoder_1_out31;
  wire [31:0] register_1_q, register_2_q, register_3_q, register_4_q, register_5_q, register_6_q,
       register_7_q, register_8_q, register_9_q, register_10_q, register_11_q, register_12_q, register_13_q,
       register_14_q, register_15_q, register_16_q, register_17_q, register_18_q, register_19_q,
       register_20_q, register_21_q, register_22_q, register_23_q, register_24_q, register_25_q,
       register_26_q, register_27_q, register_28_q, register_29_q, register_30_q, register_31_q,
       register_32_q;

  Decoder #(.select(5), .enable("false")) decoder_1 (
    .out0(decoder_1_out0), .out1(decoder_1_out1), .out2(decoder_1_out2), .out3(decoder_1_out3),
    .out4(decoder_1_out4), .out5(decoder_1_out5), .out6(decoder_1_out6), .out7(decoder_1_out7),
    .out8(decoder_1_out8), .out9(decoder_1_out9), .out10(decoder_1_out10), .out11(decoder_1_out11),
    .out12(decoder_1_out12), .out13(decoder_1_out13), .out14(decoder_1_out14), .out15(decoder_1_out15),
    .out16(decoder_1_out16), .out17(decoder_1_out17), .out18(decoder_1_out18), .out19(decoder_1_out19),
    .out20(decoder_1_out20), .out21(decoder_1_out21), .out22(decoder_1_out22), .out23(decoder_1_out23),
    .out24(decoder_1_out24), .out25(decoder_1_out25), .out26(decoder_1_out26), .out27(decoder_1_out27),
    .out28(decoder_1_out28), .out29(decoder_1_out29), .out30(decoder_1_out30), .out31(decoder_1_out31),
    .sel(Write_Reg));
  and and_1 (and_1_out, in_4, CLK, decoder_1_out0);
  and and_2 (and_2_out, in_4, CLK, decoder_1_out1);
  and and_3 (and_3_out, in_4, CLK, decoder_1_out2);
  and and_4 (and_4_out, in_4, CLK, decoder_1_out3);
  and and_5 (and_5_out, in_4, CLK, decoder_1_out4);
  and and_6 (and_6_out, in_4, CLK, decoder_1_out5);
  and and_7 (and_7_out, in_4, CLK, decoder_1_out6);
  and and_8 (and_8_out, in_4, CLK, decoder_1_out7);
  and and_9 (and_9_out, in_4, CLK, decoder_1_out8);
  and and_10 (and_10_out, in_4, CLK, decoder_1_out9);
  and and_11 (and_11_out, in_4, CLK, decoder_1_out10);
  and and_12 (and_12_out, in_4, CLK, decoder_1_out11);
  and and_13 (and_13_out, in_4, CLK, decoder_1_out12);
  and and_14 (and_14_out, in_4, CLK, decoder_1_out13);
  and and_15 (and_15_out, in_4, CLK, decoder_1_out14);
  and and_16 (and_16_out, in_4, CLK, decoder_1_out15);
  and and_17 (and_17_out, in_4, CLK, decoder_1_out16);
  and and_18 (and_18_out, in_4, CLK, decoder_1_out17);
  and and_19 (and_19_out, in_4, CLK, decoder_1_out18);
  and and_20 (and_20_out, in_4, CLK, decoder_1_out19);
  and and_21 (and_21_out, in_4, CLK, decoder_1_out20);
  and and_22 (and_22_out, in_4, CLK, decoder_1_out21);
  and and_23 (and_23_out, in_4, CLK, decoder_1_out22);
  and and_24 (and_24_out, in_4, CLK, decoder_1_out23);
  and and_25 (and_25_out, in_4, CLK, decoder_1_out24);
  and and_26 (and_26_out, in_4, CLK, decoder_1_out25);
  and and_27 (and_27_out, in_4, CLK, decoder_1_out26);
  and and_28 (and_28_out, in_4, CLK, decoder_1_out27);
  and and_29 (and_29_out, in_4, CLK, decoder_1_out28);
  and and_30 (and_30_out, in_4, CLK, decoder_1_out29);
  and and_31 (and_31_out, in_4, CLK, decoder_1_out30);
  and and_32 (and_32_out, in_4, CLK, decoder_1_out31);
  Register #(.width(32)) register_1 (.D(Write_Data), .Q(register_1_q), .clk(and_1_out));  // open: en, clr
  Register #(.width(32)) register_2 (.D(Write_Data), .Q(register_2_q), .clk(and_2_out));  // open: en, clr
  Register #(.width(32)) register_3 (.D(Write_Data), .Q(register_3_q), .clk(and_3_out));  // open: en, clr
  Register #(.width(32)) register_4 (.D(Write_Data), .Q(register_4_q), .clk(and_4_out));  // open: en, clr
  Register #(.width(32)) register_5 (.D(Write_Data), .Q(register_5_q), .clk(and_5_out));  // open: en, clr
  Register #(.width(32)) register_6 (.D(Write_Data), .Q(register_6_q), .clk(and_6_out));  // open: en, clr
  Register #(.width(32)) register_7 (.D(Write_Data), .Q(register_7_q), .clk(and_7_out));  // open: en, clr
  Register #(.width(32)) register_8 (.D(Write_Data), .Q(register_8_q), .clk(and_8_out));  // open: en, clr
  Register #(.width(32)) register_9 (.D(Write_Data), .Q(register_9_q), .clk(and_9_out));  // open: en, clr
  Register #(.width(32)) register_10 (.D(Write_Data), .Q(register_10_q), .clk(and_10_out));  // open: en, clr
  Register #(.width(32)) register_11 (.D(Write_Data), .Q(register_11_q), .clk(and_11_out));  // open: en, clr
  Register #(.width(32)) register_12 (.D(Write_Data), .Q(register_12_q), .clk(and_12_out));  // open: en, clr
  Register #(.width(32)) register_13 (.D(Write_Data), .Q(register_13_q), .clk(and_13_out));  // open: en, clr
  Register #(.width(32)) register_14 (.D(Write_Data), .Q(register_14_q), .clk(and_14_out));  // open: en, clr
  Register #(.width(32)) register_15 (.D(Write_Data), .Q(register_15_q), .clk(and_15_out));  // open: en, clr
  Register #(.width(32)) register_16 (.D(Write_Data), .Q(register_16_q), .clk(and_16_out));  // open: en, clr
  Register #(.width(32)) register_17 (.D(Write_Data), .Q(register_17_q), .clk(and_17_out));  // open: en, clr
  Register #(.width(32)) register_18 (.D(Write_Data), .Q(register_18_q), .clk(and_18_out));  // open: en, clr
  Register #(.width(32)) register_19 (.D(Write_Data), .Q(register_19_q), .clk(and_19_out));  // open: en, clr
  Register #(.width(32)) register_20 (.D(Write_Data), .Q(register_20_q), .clk(and_20_out));  // open: en, clr
  Register #(.width(32)) register_21 (.D(Write_Data), .Q(register_21_q), .clk(and_21_out));  // open: en, clr
  Register #(.width(32)) register_22 (.D(Write_Data), .Q(register_22_q), .clk(and_22_out));  // open: en, clr
  Register #(.width(32)) register_23 (.D(Write_Data), .Q(register_23_q), .clk(and_23_out));  // open: en, clr
  Register #(.width(32)) register_24 (.D(Write_Data), .Q(register_24_q), .clk(and_24_out));  // open: en, clr
  Register #(.width(32)) register_25 (.D(Write_Data), .Q(register_25_q), .clk(and_25_out));  // open: en, clr
  Register #(.width(32)) register_26 (.D(Write_Data), .Q(register_26_q), .clk(and_26_out));  // open: en, clr
  Register #(.width(32)) register_27 (.D(Write_Data), .Q(register_27_q), .clk(and_27_out));  // open: en, clr
  Register #(.width(32)) register_28 (.D(Write_Data), .Q(register_28_q), .clk(and_28_out));  // open: en, clr
  Register #(.width(32)) register_29 (.D(Write_Data), .Q(register_29_q), .clk(and_29_out));  // open: en, clr
  Register #(.width(32)) register_30 (.D(Write_Data), .Q(register_30_q), .clk(and_30_out));  // open: en, clr
  Register #(.width(32)) register_31 (.D(Write_Data), .Q(register_31_q), .clk(and_31_out));  // open: en, clr
  Register #(.width(32)) register_32 (.D(Write_Data), .Q(register_32_q), .clk(and_32_out));  // open: en, clr
  Multiplexer #(.select(5), .width(32), .enable("false")) multiplexer_1 (
    .in0(register_1_q), .in1(register_2_q), .in2(register_3_q), .in3(register_4_q), .in4(register_5_q),
    .in5(register_6_q), .in6(register_7_q), .in7(register_8_q), .in8(register_9_q), .in9(register_10_q),
    .in10(register_11_q), .in11(register_12_q), .in12(register_13_q), .in13(register_14_q),
    .in14(register_15_q), .in15(register_16_q), .in16(register_17_q), .in17(register_18_q),
    .in18(register_19_q), .in19(register_20_q), .in20(register_21_q), .in21(register_22_q),
    .in22(register_23_q), .in23(register_24_q), .in24(register_25_q), .in25(register_26_q),
    .in26(register_27_q), .in27(register_28_q), .in28(register_29_q), .in29(register_30_q),
    .in30(register_31_q), .in31(register_32_q), .out(out_7), .sel(Read_Reg_Num_1));
  Multiplexer #(.select(5), .width(32), .enable("false")) multiplexer_2 (
    .in0(register_1_q), .in1(register_2_q), .in2(register_3_q), .in3(register_4_q), .in4(register_5_q),
    .in5(register_6_q), .in6(register_7_q), .in7(register_8_q), .in8(register_9_q), .in9(register_10_q),
    .in10(register_11_q), .in11(register_12_q), .in12(register_13_q), .in13(register_14_q),
    .in14(register_15_q), .in15(register_16_q), .in16(register_17_q), .in17(register_18_q),
    .in18(register_19_q), .in19(register_20_q), .in20(register_21_q), .in21(register_22_q),
    .in22(register_23_q), .in23(register_24_q), .in24(register_25_q), .in25(register_26_q),
    .in26(register_27_q), .in27(register_28_q), .in28(register_29_q), .in29(register_30_q),
    .in30(register_31_q), .in31(register_32_q), .out(out_8), .sel(Read_Reg_Num_2));

  // Notes on the sheet:
  //   Reg Write
  //   X0
  //   X1
  //   X2
  //   X3
  //   X4
  //   X5
  //   X6
  //   X7
  //   X8
  //   X9
  //   X10
  //   X11
  //   X12
  //   X13
  //   X14
  //   Read Data 1
  //   Read Data 2
endmodule

// Inst_Split
module InstructionSplitter (
  input  [31:0] in_1,
  output _28,
  output [10:0] _31_21,
  output [4:0] _20_16,
  output [4:0] out_5,
  output [4:0] _9_5
);


  assign _9_5 = in_1[4:0];
  assign _20_16 = in_1[20:16];
  assign _28 = in_1[28];
  assign _31_21 = in_1[31:21];
  assign out_5 = in_1[9:5];

  // Notes on the sheet:
  //   4-0
endmodule

module IF_ID (
  input  in_1,
  input  [31:0] in_2,
  input  [31:0] in_3,
  input  CLK,
  input  IF_ID_Flush,
  output [31:0] out_6,
  output [31:0] out_7
);

  wire register_3_q;

  Register #(.width(32)) register_1 (.D(in_2), .en(in_1), .Q(out_6), .clk(CLK));  // open: clr
  Register #(.width(32)) register_2 (.D(in_3), .en(in_1), .Q(out_7), .clk(CLK), .clr(register_3_q));
  Register #(.width(1)) register_3 (.D(IF_ID_Flush), .Q(register_3_q), .clk(CLK));  // open: en, clr

  // Notes on the sheet:
  //   PC
  //   INST
  //   IF/ID Write
endmodule

module ID_EX (
  input  [10:0] in_1,
  input  [31:0] in_2,
  input  [31:0] in_3,
  input  [31:0] in_4,
  input  [31:0] in_5,
  input  [4:0] Rn,
  input  [4:0] Rm,
  input  [4:0] in_8,
  input  CLK,
  output [10:0] out_10,
  output [31:0] out_11,
  output [31:0] out_12,
  output [31:0] out_13,
  output [31:0] out_14,
  output [4:0] out_15,
  output [4:0] out_16,
  output [4:0] out_17
);

  Register #(.width(11)) register_1 (.D(in_1), .Q(out_10), .clk(CLK));  // open: en, clr
  Register #(.width(32)) register_2 (.D(in_2), .Q(out_11), .clk(CLK));  // open: en, clr
  Register #(.width(32)) register_3 (.D(in_3), .Q(out_12), .clk(CLK));  // open: en, clr
  Register #(.width(32)) register_4 (.D(in_4), .Q(out_13), .clk(CLK));  // open: en, clr
  Register #(.width(32)) register_5 (.D(in_5), .Q(out_14), .clk(CLK));  // open: en, clr
  Register #(.width(5)) register_6 (.D(Rn), .Q(out_15), .clk(CLK));  // open: en, clr
  Register #(.width(5)) register_7 (.D(Rm), .Q(out_16), .clk(CLK));  // open: en, clr
  Register #(.width(5)) register_8 (.D(in_8), .Q(out_17), .clk(CLK));  // open: en, clr

  // Notes on the sheet:
  //   ALU CONTROL
  //   PC
  //   Read 1
  //   Read 2
  //   Sign Extend
  //   Write Reg (Rd)
endmodule

module MEM_WB (
  input  [31:0] in_1,
  input  [31:0] in_2,
  input  [4:0] in_3,
  input  CLK,
  output [31:0] out_5,
  output [31:0] out_6,
  output [4:0] out_7
);

  Register #(.width(32)) register_1 (.D(in_1), .Q(out_5), .clk(CLK));  // open: en, clr
  Register #(.width(32)) register_2 (.D(in_2), .Q(out_6), .clk(CLK));  // open: en, clr
  Register #(.width(5)) register_3 (.D(in_3), .Q(out_7), .clk(CLK));  // open: en, clr

  // Notes on the sheet:
  //   Read Data
  //   ALU Result
  //   Write Reg
endmodule

module EX_MEM (
  input  [31:0] in_1,
  input  [31:0] in_2,
  input  Zero,
  input  [31:0] in_4,
  input  [4:0] in_5,
  input  CLK,
  output [31:0] out_7,
  output [31:0] out_8,
  output out_9,
  output [31:0] out_10,
  output [4:0] out_11
);

  Register #(.width(32)) register_1 (.D(in_1), .Q(out_7), .clk(CLK));  // open: en, clr
  Register #(.width(32)) register_2 (.D(in_2), .Q(out_8), .clk(CLK));  // open: en, clr
  Register #(.width(1)) register_3 (.D(Zero), .Q(out_9), .clk(CLK));  // open: en, clr
  Register #(.width(32)) register_4 (.D(in_4), .Q(out_10), .clk(CLK));  // open: en, clr
  Register #(.width(5)) register_5 (.D(in_5), .Q(out_11), .clk(CLK));  // open: en, clr

  // Notes on the sheet:
  //   PC Branch
  //   ALU Result
  //   Write Data
  //   Write Reg
endmodule

// PC
module PC_without_Shift_Adder (
  input  in_1,
  input  [31:0] in_2,
  input  MUX_Control,
  input  Undef_Inst,
  input  CLK,
  input  Reset,
  output [31:0] out_7
);

  wire [31:0] adder_1_out, multiplexer_1_out;

  Register #(.width(32)) register_1 (.D(multiplexer_1_out), .en(in_1), .Q(out_7), .clk(CLK), .clr(Reset));
  Adder #(.width(32)) adder_1 (.a(out_7), .b(32'h4), .out(adder_1_out));  // open: cin, cout
  Multiplexer #(.select(2), .width(32), .enable("false")) multiplexer_1 (
    .in0(adder_1_out), .in1(in_2), .in2(32'h100), .in3(32'h100), .out(multiplexer_1_out),
    .sel({Undef_Inst, MUX_Control}));

  // Notes on the sheet:
  //   PC Output
  //   Adder Result
  //   Undef Inst PC Set
endmodule

module WB (
  input  RegWrite,
  input  MemtoReg,
  input  CLK,
  output out_4,
  output out_5
);

  Register #(.width(1)) register_1 (.D(RegWrite), .Q(out_4), .clk(CLK));  // open: en, clr
  Register #(.width(1)) register_2 (.D(MemtoReg), .Q(out_5), .clk(CLK));  // open: en, clr
endmodule

module M (
  input  Branch,
  input  MemRead,
  input  MemWrite,
  input  CLK,
  output out_5,
  output out_6,
  output out_7
);

  Register #(.width(1)) register_1 (.D(Branch), .Q(out_5), .clk(CLK));  // open: en, clr
  Register #(.width(1)) register_2 (.D(MemRead), .Q(out_6), .clk(CLK));  // open: en, clr
  Register #(.width(1)) register_3 (.D(MemWrite), .Q(out_7), .clk(CLK));  // open: en, clr
endmodule

module EX (
  input  [1:0] ALUOp,
  input  ALUSrc,
  input  CLK,
  output [1:0] out_4,
  output out_5
);

  Register #(.width(2)) register_1 (.D(ALUOp), .Q(out_4), .clk(CLK));  // open: en, clr
  Register #(.width(1)) register_2 (.D(ALUSrc), .Q(out_5), .clk(CLK));  // open: en, clr
endmodule

// Forward
module Forwarding_Unit (
  input  MEM_WB_RegWrite,
  input  in_2,
  input  [4:0] ID_EX_Rn,
  input  [4:0] ID_EX_Rm,
  input  [4:0] in_5,
  input  [4:0] in_6,
  output [1:0] out_7,
  output [1:0] out_8
);

  wire and_1_out, and_2_out, and_3_out, and_4_out, and_7_out, and_8_out, and_9_out, and_10_out,
       comparator_1_eq, comparator_2_eq, comparator_3_eq, comparator_4_eq, comparator_5_eq, not_1_out,
       not_2_out, not_3_out, not_4_out;

  Comparator #(.width(5)) comparator_1 (.a(ID_EX_Rn), .b(in_5), .eq(comparator_1_eq));  // open: gt, lt
  Comparator #(.width(5)) comparator_2 (.a(in_5), .b(ID_EX_Rm), .eq(comparator_2_eq));  // open: gt, lt
  Comparator #(.width(5)) comparator_3 (.a(in_6), .b(ID_EX_Rn), .eq(comparator_3_eq));  // open: gt, lt
  Comparator #(.width(5)) comparator_4 (.a(in_6), .b(ID_EX_Rm), .eq(comparator_4_eq));  // open: gt, lt
  Comparator #(.width(5)) comparator_5 (.a(in_5), .b(ID_EX_Rn), .eq(comparator_5_eq));  // open: gt, lt
  and and_1 (and_1_out, in_5[0], in_5[1], in_5[2], in_5[3], in_5[4]);
  not not_1 (not_1_out, and_1_out);
  not not_2 (not_2_out, and_2_out);
  and and_2 (and_2_out, in_6[0], in_6[1], in_6[2], in_6[3], in_6[4]);
  not not_3 (not_3_out, and_3_out);
  and and_3 (and_3_out, in_2, not_1_out, comparator_5_eq);
  and and_4 (and_4_out, in_2, not_1_out, comparator_2_eq);
  not not_4 (not_4_out, and_4_out);
  and and_5 (out_7[1], in_2, comparator_1_eq, not_1_out);
  and and_6 (out_8[1], in_2, not_1_out, comparator_2_eq);
  and and_7 (and_7_out, MEM_WB_RegWrite, not_2_out, comparator_3_eq);
  and and_8 (and_8_out, MEM_WB_RegWrite, not_2_out, comparator_4_eq);
  or or_1 (out_7[0], and_7_out, and_9_out);
  or or_2 (out_8[0], and_8_out, and_10_out);
  and and_9 (and_9_out, MEM_WB_RegWrite, not_2_out, not_3_out, comparator_3_eq);
  and and_10 (and_10_out, MEM_WB_RegWrite, not_2_out, not_4_out, comparator_4_eq);

  // Notes on the sheet:
  //   EX/MEM RegWrite
  //   EX/MEM Rd
  //   MEM/WB Rd
  //   Forward A MSB
  //   Forward A LSB
  //   Forward B MSB
  //   Forward B LSB
endmodule

module Hazard (
  input  in_1,
  input  [4:0] in_2,
  input  [4:0] in_3,
  input  [4:0] in_4,
  output PCWrite,
  output IF_IDWrite,
  output PipeStall
);

  wire comparator_1_eq, comparator_2_eq, or_1_out;

  Comparator #(.width(5)) comparator_1 (.a(in_2), .b(in_4), .eq(comparator_1_eq));  // open: gt, lt
  Comparator #(.width(5)) comparator_2 (.a(in_3), .b(in_4), .eq(comparator_2_eq));  // open: gt, lt
  or or_1 (or_1_out, comparator_1_eq, comparator_2_eq);
  not not_1 (IF_IDWrite, PipeStall);
  and and_1 (PipeStall, in_1, or_1_out);

  assign PCWrite = IF_IDWrite;

  // Notes on the sheet:
  //   IF/ID Rm
  //   IF/ID Rn
  //   ID/EX Rd
  //   ID/EX MemRead
endmodule

// Mux
module HZD_MUX_Unit (
  input  in_1,
  input  in_2,
  output out_3
);

  Multiplexer #(.enable("false")) multiplexer_1 (.in0(in_2), .in1(1'b0), .out(out_3), .sel(in_1));
endmodule

module HZD_2B_MUX (
  input  in_1,
  input  [1:0] in_2,
  output [1:0] out_3
);

  Multiplexer #(.width(2), .enable("false")) multiplexer_1 (.in0(in_2), .in1(2'b00), .out(out_3), .sel(in_1));
endmodule

// 2Mux
module HZD_WB_MUX (
  input  in_1,
  input  in_2,
  input  in_3,
  output out_4,
  output out_5
);

  HZD_MUX_Unit hzd_mux_unit_1 (.in_1(in_1), .in_2(in_2), .out_3(out_4));
  HZD_MUX_Unit hzd_mux_unit_2 (.in_1(in_1), .in_2(in_3), .out_3(out_5));
endmodule

// 3Mux
module HZD_M_MUX (
  input  in_1,
  input  in_2,
  input  in_3,
  input  in_4,
  output out_5,
  output out_6,
  output out_7
);

  HZD_MUX_Unit hzd_mux_unit_1 (.in_1(in_1), .in_2(in_2), .out_3(out_5));
  HZD_MUX_Unit hzd_mux_unit_2 (.in_1(in_1), .in_2(in_3), .out_3(out_6));
  HZD_MUX_Unit hzd_mux_unit_3 (.in_1(in_1), .in_2(in_4), .out_3(out_7));
endmodule

// EXMux
module HZD_EX_MUX (
  input  in_1,
  input  [1:0] in_2,
  input  in_3,
  output [1:0] out_4,
  output out_5
);

  HZD_2B_MUX hzd_2b_mux_1 (.in_1(in_1), .in_2(in_2), .out_3(out_4));
  HZD_MUX_Unit hzd_mux_unit_1 (.in_1(in_1), .in_2(in_3), .out_3(out_5));
endmodule

// Zero
module Zero_Check (
  input  [31:0] in_1,
  output Zero
);

  nor nor_1 (Zero, in_1[0], in_1[1], in_1[2], in_1[3], in_1[4], in_1[5], in_1[6], in_1[7], in_1[8], in_1[9], in_1[10], in_1[11], in_1[12], in_1[13], in_1[14], in_1[15], in_1[16], in_1[17], in_1[18], in_1[19], in_1[20], in_1[21], in_1[22], in_1[23], in_1[24], in_1[25], in_1[26], in_1[27], in_1[28], in_1[29], in_1[30], in_1[31]);
endmodule

module Simple_LegV8 (
  input  Reset
);

  wire and_1_out, clock_1_out, control_1_alusrc, control_1_branch, control_1_memread, control_1_memtoreg,
       control_1_memwrite, control_1_out_10, control_1_regwrite, ex_1_out_5, hazard_1_if_idwrite,
       hazard_1_pcwrite, hazard_1_pipestall, hzd_ex_mux_1_out_5, hzd_m_mux_1_out_5, hzd_m_mux_1_out_6,
       hzd_m_mux_1_out_7, hzd_m_mux_2_out_5, hzd_m_mux_2_out_6, hzd_m_mux_2_out_7, hzd_wb_mux_1_out_4,
       hzd_wb_mux_1_out_5, hzd_wb_mux_2_out_4, hzd_wb_mux_2_out_5, instructionsplitter_1__28, m_1_out_5,
       m_1_out_6, m_1_out_7, m_2_out_6, m_2_out_7, n32b_alu_1_out_5, or_1_out, or_2_out, register_1_q,
       wb_1_out_4, wb_1_out_5, wb_2_out_4, wb_2_out_5, wb_3_out_4, wb_3_out_5, zero_check_1_zero;
  wire [1:0] control_1_aluop0, ex_1_out_4, forwarding_unit_1_out_7, forwarding_unit_1_out_8,
       hzd_ex_mux_1_out_4;
  wire [3:0] alu_control_1_out_3;
  wire [4:0] ex_mem_1_out_11, id_ex_1_out_15, id_ex_1_out_16, id_ex_1_out_17, instructionsplitter_1__9_5,
       instructionsplitter_1__20_16, instructionsplitter_1_out_5, mem_wb_1_out_7, multiplexer_1_out;
  wire [10:0] id_ex_1_out_10, instruction_cutoff_1_out_2, instructionsplitter_1__31_21;
  wire [31:0] adder_1_out, adder_2_out, data_memory_1_out_6, ex_mem_1_out_7, ex_mem_1_out_8, ex_mem_1_out_10,
       id_ex_1_out_11, id_ex_1_out_12, id_ex_1_out_13, id_ex_1_out_14, if_id_1_out_6, if_id_1_out_7,
       instruction_memory_1_out_2, mem_wb_1_out_5, mem_wb_1_out_6, multiplexer_2_out, multiplexer_3_out,
       multiplexer_4_out, multiplexer_5_out, n32b_alu_1_out_4, pc_without_shift_adder_1_out_7,
       register_file_1_out_7, register_file_1_out_8, shift_left_2_1_out_2, sign_extender_1_out_2;

  Clock clock_1 (.out(clock_1_out));
  PC_without_Shift_Adder pc_without_shift_adder_1 (
    .in_2(adder_1_out), .CLK(clock_1_out), .Reset(Reset), .out_7(pc_without_shift_adder_1_out_7),
    .MUX_Control(and_1_out), .in_1(hazard_1_pcwrite), .Undef_Inst(control_1_out_10));
  Instruction_memory instruction_memory_1 (.in_1(pc_without_shift_adder_1_out_7), .out_2(instruction_memory_1_out_2));
  IF_ID if_id_1 (
    .in_2(pc_without_shift_adder_1_out_7), .in_3(instruction_memory_1_out_2), .CLK(clock_1_out),
    .out_6(if_id_1_out_6), .out_7(if_id_1_out_7), .in_1(hazard_1_if_idwrite), .IF_ID_Flush(and_1_out));
  Adder #(.width(32)) adder_1 (.a(if_id_1_out_6), .b(shift_left_2_1_out_2), .out(adder_1_out));  // open: cin, cout
  InstructionSplitter instructionsplitter_1 (
    .in_1(if_id_1_out_7), ._31_21(instructionsplitter_1__31_21), ._20_16(instructionsplitter_1__20_16),
    .out_5(instructionsplitter_1_out_5), ._9_5(instructionsplitter_1__9_5), ._28(instructionsplitter_1__28));
  Instruction_Cutoff instruction_cutoff_1 (.in_1(if_id_1_out_7), .out_2(instruction_cutoff_1_out_2));
  Sign_Extender sign_extender_1 (.out_2(sign_extender_1_out_2), .in_1(if_id_1_out_7));
  Shift_Left_2 shift_left_2_1 (.in_1(sign_extender_1_out_2), .out_2(shift_left_2_1_out_2));
  or or_1 (or_1_out, control_1_out_10, control_1_branch);
  Hazard hazard_1 (
    .in_1(m_1_out_6), .in_2(instructionsplitter_1__20_16), .in_3(instructionsplitter_1_out_5),
    .in_4(id_ex_1_out_17), .PCWrite(hazard_1_pcwrite), .IF_IDWrite(hazard_1_if_idwrite),
    .PipeStall(hazard_1_pipestall));
  Control control_1 (
    .in_1(instructionsplitter_1__31_21), .Branch(control_1_branch), .MemRead(control_1_memread),
    .MemtoReg(control_1_memtoreg), .ALUOp0(control_1_aluop0), .MemWrite(control_1_memwrite),
    .ALUSrc(control_1_alusrc), .RegWrite(control_1_regwrite), .out_10(control_1_out_10));  // open: Reg2Loc
  Multiplexer #(.width(5), .enable("false")) multiplexer_1 (
    .in0(instructionsplitter_1__20_16), .in1(instructionsplitter_1__9_5), .out(multiplexer_1_out),
    .sel(instructionsplitter_1__28));
  and and_1 (and_1_out, or_1_out, zero_check_1_zero);
  Zero_Check zero_check_1 (.in_1(register_file_1_out_8), .Zero(zero_check_1_zero));
  or or_2 (or_2_out, control_1_out_10, hazard_1_pipestall);
  HZD_EX_MUX hzd_ex_mux_1 (
    .in_1(or_2_out), .in_2(control_1_aluop0), .in_3(control_1_alusrc), .out_4(hzd_ex_mux_1_out_4),
    .out_5(hzd_ex_mux_1_out_5));
  Register_File register_file_1 (
    .Read_Reg_Num_1(instructionsplitter_1_out_5), .Read_Reg_Num_2(multiplexer_1_out),
    .Write_Data(multiplexer_5_out), .in_4(wb_3_out_4), .Write_Reg(mem_wb_1_out_7),
    .out_7(register_file_1_out_7), .out_8(register_file_1_out_8), .CLK(clock_1_out));
  HZD_M_MUX hzd_m_mux_1 (
    .in_1(or_2_out), .in_2(control_1_branch), .in_3(control_1_memread), .in_4(control_1_memwrite),
    .out_5(hzd_m_mux_1_out_5), .out_6(hzd_m_mux_1_out_6), .out_7(hzd_m_mux_1_out_7));
  HZD_WB_MUX hzd_wb_mux_1 (
    .in_1(or_2_out), .in_2(control_1_regwrite), .in_3(control_1_memtoreg), .out_4(hzd_wb_mux_1_out_4),
    .out_5(hzd_wb_mux_1_out_5));
  WB wb_1 (
    .RegWrite(hzd_wb_mux_1_out_4), .MemtoReg(hzd_wb_mux_1_out_5), .CLK(clock_1_out), .out_4(wb_1_out_4),
    .out_5(wb_1_out_5));
  M m_1 (
    .Branch(hzd_m_mux_1_out_5), .MemRead(hzd_m_mux_1_out_6), .MemWrite(hzd_m_mux_1_out_7), .CLK(clock_1_out),
    .out_5(m_1_out_5), .out_6(m_1_out_6), .out_7(m_1_out_7));
  EX ex_1 (
    .ALUOp(hzd_ex_mux_1_out_4), .ALUSrc(hzd_ex_mux_1_out_5), .CLK(clock_1_out), .out_4(ex_1_out_4),
    .out_5(ex_1_out_5));
  ID_EX id_ex_1 (
    .in_2(if_id_1_out_6), .in_3(register_file_1_out_7), .in_4(register_file_1_out_8),
    .in_5(sign_extender_1_out_2), .in_8(instructionsplitter_1__9_5), .CLK(clock_1_out),
    .out_11(id_ex_1_out_11), .out_12(id_ex_1_out_12), .out_13(id_ex_1_out_13), .out_14(id_ex_1_out_14),
    .out_17(id_ex_1_out_17), .in_1(instruction_cutoff_1_out_2), .out_10(id_ex_1_out_10),
    .Rn(instructionsplitter_1_out_5), .out_15(id_ex_1_out_15), .Rm(instructionsplitter_1__20_16),
    .out_16(id_ex_1_out_16));
  Adder #(.width(32)) adder_2 (.a(shift_left_2_1_out_2), .b(id_ex_1_out_11), .out(adder_2_out));  // open: cin, cout
  ALU_Control alu_control_1 (.I_30(ex_1_out_4), .I_24(id_ex_1_out_10), .out_3(alu_control_1_out_3));
  Multiplexer #(.select(2), .width(32), .enable("false")) multiplexer_2 (
    .in0(id_ex_1_out_12), .in1(multiplexer_5_out), .in2(ex_mem_1_out_8), .out(multiplexer_2_out),
    .sel(forwarding_unit_1_out_7));  // open: in3
  Multiplexer #(.select(2), .width(32), .enable("false")) multiplexer_3 (
    .in0(id_ex_1_out_13), .in1(multiplexer_5_out), .in2(ex_mem_1_out_8), .out(multiplexer_3_out),
    .sel(forwarding_unit_1_out_8));  // open: in3
  Multiplexer #(.width(32), .enable("false")) multiplexer_4 (
    .in0(multiplexer_3_out), .in1(id_ex_1_out_14), .out(multiplexer_4_out), .sel(ex_1_out_5));
  HZD_M_MUX hzd_m_mux_2 (
    .in_1(or_2_out), .in_2(m_1_out_5), .in_3(m_1_out_6), .in_4(m_1_out_7), .out_5(hzd_m_mux_2_out_5),
    .out_6(hzd_m_mux_2_out_6), .out_7(hzd_m_mux_2_out_7));
  Register #(.width(1)) register_1 (.D(or_2_out), .Q(register_1_q), .clk(clock_1_out));  // open: en, clr
  HZD_WB_MUX hzd_wb_mux_2 (
    .in_1(or_2_out), .in_2(wb_1_out_4), .in_3(wb_1_out_5), .out_4(hzd_wb_mux_2_out_4),
    .out_5(hzd_wb_mux_2_out_5));
  Register #(.width(32)) register_2 (.D(id_ex_1_out_11), .en(register_1_q), .clk(clock_1_out));  // open: Q, clr
  _32B_ALU u_32b_alu_1 (
    .out_5(n32b_alu_1_out_5), .out_4(n32b_alu_1_out_4), .in_2(multiplexer_4_out), .in_3(multiplexer_2_out),
    .LSB(alu_control_1_out_3));
  Forwarding_Unit forwarding_unit_1 (
    .MEM_WB_RegWrite(wb_3_out_4), .in_2(wb_2_out_4), .ID_EX_Rn(id_ex_1_out_15), .ID_EX_Rm(id_ex_1_out_16),
    .in_5(ex_mem_1_out_11), .in_6(mem_wb_1_out_7), .out_7(forwarding_unit_1_out_7),
    .out_8(forwarding_unit_1_out_8));
  WB wb_2 (
    .RegWrite(hzd_wb_mux_2_out_4), .MemtoReg(hzd_wb_mux_2_out_5), .CLK(clock_1_out), .out_4(wb_2_out_4),
    .out_5(wb_2_out_5));
  M m_2 (
    .Branch(hzd_m_mux_2_out_5), .MemRead(hzd_m_mux_2_out_6), .MemWrite(hzd_m_mux_2_out_7), .CLK(clock_1_out),
    .out_6(m_2_out_6), .out_7(m_2_out_7));  // open: out_5
  EX_MEM ex_mem_1 (
    .in_1(adder_2_out), .in_2(n32b_alu_1_out_4), .Zero(n32b_alu_1_out_5), .in_4(id_ex_1_out_13),
    .in_5(id_ex_1_out_17), .CLK(clock_1_out), .out_7(ex_mem_1_out_7), .out_8(ex_mem_1_out_8),
    .out_10(ex_mem_1_out_10), .out_11(ex_mem_1_out_11));  // open: out_9
  Data_Memory data_memory_1 (
    .in_2(ex_mem_1_out_10), .MemWrite(m_2_out_7), .MemRead(m_2_out_6), .CLK(clock_1_out),
    .out_6(data_memory_1_out_6), .in_1(ex_mem_1_out_8));
  WB wb_3 (.RegWrite(wb_2_out_4), .MemtoReg(wb_2_out_5), .CLK(clock_1_out), .out_4(wb_3_out_4), .out_5(wb_3_out_5));
  MEM_WB mem_wb_1 (
    .in_1(ex_mem_1_out_8), .in_2(data_memory_1_out_6), .in_3(ex_mem_1_out_11), .CLK(clock_1_out),
    .out_5(mem_wb_1_out_5), .out_6(mem_wb_1_out_6), .out_7(mem_wb_1_out_7));
  Multiplexer #(.width(32), .enable("false")) multiplexer_5 (
    .in0(mem_wb_1_out_5), .in1(mem_wb_1_out_6), .out(multiplexer_5_out), .sel(wb_3_out_5));

  // Notes on the sheet:
  //   MUX
  //   CLK
  //   Add Result
  //   IF Flush
  //   31-21
  //   20-16
  //   9-5
  //   Write Reg
  //   4-0
  //   28
  //   Read Reg 1
  //   Read Reg 2
  //   Write Reg
  //   Read Data 1
  //   Read Data 2
  //   Write Data
  //   Reg Write
  //   ELR
  //   ALU Result
  //   Zero
  //   Read
  //   Write
  //   Address
  //   Write Data
  //   Clock
  //   Write Data
endmodule
